// Logisim project askhsh_1.circ as structural Verilog: 7 circuits, main circuit main
module main (
  input  [7:0] A,
  input  [7:0] B,
  input  [2:0] Sel,
  output [7:0] Result,
  output Cout
);

  wire [7:0] and_1_out, not_1_out, xor_1_out;
  wire [8:0] fa_9bit_1_out_3, FA_out_3, Mux2x1_result;

  Hex_Digit_Display hex_digit_display_1 (.value(Result[7:4]));  // open: dp
  Hex_Digit_Display hex_digit_display_2 (.value(Result[3:0]), .dp(Result[0]));
  Hex_Digit_Display hex_digit_display_3 (.value({1'b0, Sel}));  // open: dp
  assign not_1_out = ~B;  // NOT_Gate not_1, 8 bits wide
  mux_2x1 Mux2x1 (.on_off(1'b1), .x1({1'b0, B}), .x2({1'b0, A}), .sel(Sel[0]), .Result(Mux2x1_result));
  FA_9BIT fa_9bit_1 (.in_1(A), .in_2(B), .out_4(fa_9bit_1_out_3[8]), .out_3(fa_9bit_1_out_3[7:0]));
  assign and_1_out = A & B;  // AND_Gate and_1, 8 bits wide
  assign xor_1_out = A ^ B;  // XOR_Gate xor_1, 8 bits wide
  Hex_Digit_Display hex_digit_display_4 (.value(FA_out_3[7:4]));  // open: dp
  FA_9BIT FA (.in_1(8'h1), .in_2(Mux2x1_result[7:0]), .out_4(FA_out_3[8]), .out_3(FA_out_3[7:0]));
  Hex_Digit_Display hex_digit_display_5 (.value(FA_out_3[3:0]), .dp(FA_out_3[0]));
  mux_3_8 MUX (
    .in_9(Sel), .in_1({9{1'b0}}), .in_2({1'b0, not_1_out}), .in_3(fa_9bit_1_out_3), .in_4({1'b0, and_1_out}),
    .in_5({1'b0, xor_1_out}), .in_6(FA_out_3), .in_7(FA_out_3), .in_8({9{1'b0}}), .out_10({Cout, Result}));
  // Pins of 1 and 4 bits meet at Result[3:0]
  // Pins of 1 and 4 bits meet at FA_out_3[3:0]

  // Notes on the sheet:
  //   A
  //   B
  //   odd = sel[0]==0
  //   6 ->B so check if even
  //   5 ->A so if it is odd
  //   5,6
  //   1
  //   2
  //   FA
  //   3
  //   4
  //   here i choose one of the 2 signals, mux needed (and convert the signals to 9bit)
  //   0,7 are 0 because theyre invalid
endmodule

module mux_2x1 (
  input  on_off,
  input  [8:0] x1,
  input  [8:0] x2,
  input  sel,
  output [8:0] Result
);

  wire [8:0] and_1_out, and_2_out, and_3_out, not_1_out;

  assign not_1_out = ~{9{sel}};  // NOT_Gate not_1, 9 bits wide
  assign and_1_out = not_1_out & {9{on_off}} & x1;  // AND_Gate and_1, 9 bits wide
  assign and_2_out = x1 & {9{on_off}} & x2;  // AND_Gate and_2, 9 bits wide
  assign and_3_out = {9{sel}} & {9{on_off}} & x2;  // AND_Gate and_3, 9 bits wide
  assign Result = and_1_out | and_2_out | and_3_out;  // OR_Gate or_1, 9 bits wide
endmodule

module mux_3_8 (
  input  [8:0] in_1,
  input  [8:0] in_2,
  input  [8:0] in_3,
  input  [8:0] in_4,
  input  [8:0] in_5,
  input  [8:0] in_6,
  input  [8:0] in_7,
  input  [8:0] in_8,
  input  [2:0] in_9,
  output [8:0] out_10
);

  wire and_1_out, and_2_out, and_3_out, and_4_out, not_1_out, not_2_out;
  wire [8:0] mux_2x1_1_result, mux_2x1_2_result, mux_2x1_3_result, mux_2x1_4_result;

  mux_2x1 mux_2x1_1 (.on_off(and_1_out), .x1(in_1), .x2(in_2), .sel(in_9[0]), .Result(mux_2x1_1_result));
  mux_2x1 mux_2x1_2 (.on_off(and_2_out), .x1(in_3), .x2(in_4), .sel(in_9[0]), .Result(mux_2x1_2_result));
  not not_1 (not_1_out, in_9[1]);
  not not_2 (not_2_out, in_9[2]);
  mux_2x1 mux_2x1_3 (.on_off(and_3_out), .x1(in_5), .x2(in_6), .sel(in_9[0]), .Result(mux_2x1_3_result));
  mux_2x1 mux_2x1_4 (.on_off(and_4_out), .x1(in_7), .x2(in_8), .sel(in_9[0]), .Result(mux_2x1_4_result));
  and and_1 (and_1_out, not_1_out, not_2_out);
  and and_2 (and_2_out, not_2_out, in_9[1]);
  and and_3 (and_3_out, in_9[2], not_1_out);
  and and_4 (and_4_out, in_9[2], in_9[1]);
  assign out_10 = mux_2x1_1_result | mux_2x1_2_result | mux_2x1_3_result | mux_2x1_4_result;  // OR_Gate or_1, 9 bits wide

  // Notes on the sheet:
  //   first 2 bits are for which mux, last is for the specific mux which of the 2 signals
  //   00 (1)
  //   01 (2)
  //   10 (3)
  //   11(4)
  //   b2'b1'
  //   b2'b1
  //   b2b1'
  //   b2b1
endmodule

module half_adder (
  input  in_1,
  input  in_2,
  output sum,
  output carry
);

  xor xor_1 (sum, in_1, in_2);
  and and_1 (carry, in_1, in_2);
endmodule

module full_adder (
  input  in_1,
  input  in_2,
  input  in_3,
  output sum,
  output carry
);

  wire half_adder_1_carry, half_adder_1_sum, half_adder_2_carry;

  half_adder half_adder_1 (.in_1(in_1), .in_2(in_2), .sum(half_adder_1_sum), .carry(half_adder_1_carry));
  half_adder half_adder_2 (.in_1(half_adder_1_sum), .in_2(in_3), .sum(sum), .carry(half_adder_2_carry));
  or or_1 (carry, half_adder_2_carry, half_adder_1_carry);
endmodule

module FA_9BIT (
  input  [7:0] in_1,
  input  [7:0] in_2,
  output [7:0] out_3,
  output out_4
);

  wire full_adder_1_carry, full_adder_2_carry, full_adder_3_carry, full_adder_4_carry, full_adder_5_carry,
       full_adder_6_carry, half_adder_1_carry;

  half_adder half_adder_1 (.in_1(in_1[0]), .in_2(in_2[0]), .sum(out_3[0]), .carry(half_adder_1_carry));
  full_adder full_adder_1 (
    .in_1(half_adder_1_carry), .in_2(in_1[1]), .in_3(in_2[1]), .sum(out_3[1]), .carry(full_adder_1_carry));
  full_adder full_adder_2 (
    .in_1(full_adder_1_carry), .in_2(in_1[2]), .in_3(in_2[2]), .sum(out_3[2]), .carry(full_adder_2_carry));
  full_adder full_adder_3 (
    .in_1(full_adder_2_carry), .in_2(in_1[3]), .in_3(in_2[3]), .sum(out_3[3]), .carry(full_adder_3_carry));
  full_adder full_adder_4 (
    .in_1(full_adder_3_carry), .in_2(in_1[4]), .in_3(in_2[4]), .sum(out_3[4]), .carry(full_adder_4_carry));
  full_adder full_adder_5 (
    .in_1(full_adder_4_carry), .in_2(in_2[5]), .in_3(in_1[5]), .sum(out_3[5]), .carry(full_adder_5_carry));
  full_adder full_adder_6 (
    .in_1(full_adder_5_carry), .in_2(in_1[6]), .in_3(in_2[6]), .sum(out_3[6]), .carry(full_adder_6_carry));
  full_adder full_adder_7 (.in_1(full_adder_6_carry), .in_2(in_1[7]), .in_3(in_2[7]), .sum(out_3[7]), .carry(out_4));
endmodule

module mainn (
  input  [7:0] in_1,
  input  [7:0] in_2,
  input  [2:0] in_3,
  output [7:0] out_4,
  output out_5
);

  main main_1 (.A(in_1), .B(in_2), .Sel(in_3), .Result(out_4), .Cout(out_5));
endmodule
