// Logisim project askhsh_2.circ as structural Verilog: 2 circuits, main circuit main
module main (
  input  SET,
  input  RESET
);

  wire and_1_out, and_2_out, and_3_out, and_4_out, CLK_out, not_1_out, or_1_out, or_2_out, or_3_out;
  wire [3:0] FF0_q;

  or or_1 (or_1_out, SET, RESET);
  Clock CLK (.out(CLK_out));
  myff FF0 (.J(not_1_out), .K(1'b1), .RESET(or_1_out), .CLK(CLK_out), .Q(FF0_q[0]));  // open: SET
  Hex_Digit_Display hex_digit_display_1 (.value(FF0_q));  // open: dp
  or or_2 (or_2_out, and_4_out, FF0_q[0]);
  and and_1 (and_1_out, not_1_out, FF0_q[0]);
  myff FF1 (.J(and_1_out), .K(or_2_out), .RESET(or_1_out), .CLK(CLK_out), .Q(FF0_q[1]));  // open: SET
  and and_2 (and_2_out, FF0_q[0], FF0_q[1]);
  myff FF2 (.SET(SET), .J(and_2_out), .K(or_3_out), .RESET(RESET), .CLK(CLK_out), .Q(FF0_q[2]));
  or or_3 (or_3_out, and_2_out, FF0_q[3]);
  and and_3 (and_3_out, and_2_out, FF0_q[2]);
  myff FF3 (.SET(SET), .J(and_3_out), .K(FF0_q[2]), .RESET(RESET), .CLK(CLK_out), .Q(FF0_q[3]));
  and and_4 (and_4_out, FF0_q[2], FF0_q[3]);
  not not_1 (not_1_out, and_4_out);
endmodule

module myff (
  input  SET,
  input  J,
  input  K,
  input  CLK,
  input  RESET,
  output Q
);

  wire and_1_out, and_2_out, not_1_out, not_2_out, or_1_out, or_2_out;

  not not_1 (not_1_out, RESET);
  or or_1 (or_1_out, SET, J);
  not not_2 (not_2_out, SET);
  and and_1 (and_1_out, or_1_out, not_1_out);
  and and_2 (and_2_out, not_2_out, K);
  or or_2 (or_2_out, and_2_out, RESET);
  J_K_Flip_Flop #(.trigger("falling")) j_k_ff_1 (
    .J(and_1_out), .K(or_2_out), .clk(CLK), .Q(Q));  // open: Qn, preset, reset
endmodule
